# Fritzing sketch DC Motor Driver schema with Relay (saved by Fritzing 0.9.2b)
breadboards: 1

parts:
  Part1 = Arduino Uno (Rev3)  # not connected
  R1 = Resistor [tolerance=±5% resistance=1k package=THT]
  U1 = RELAY [package=relay-t9a-2]
  M1 = DC Motor
  V1 = DC Power [voltage=5]
  V2 = DC Power [voltage=5]
  Q1 = TRANSISTOR_NPN [package=to-92-ammo]
  D1 = Rectifier Diode [part_number=1N4001 package="300 mil [THT]"]

nets:
  N1: R1.Pin_1, Q1.B
  N2: U1.COIL1, V1.V-, D1.cathode
  N3: U1.COIL2, Q1.C, D1.anode
  N4: U1.MAIN, V2.V-
  N5: U1.NC, M1.pin_2
  N6: M1.pin_1, V2.V+
  GND: Q1.E
