# Fritzing sketch Wireless com test (saved by Fritzing 0.9.2b)
breadboards: 1

parts:
  Arduino = Arduino Uno (Rev3) - ICSP
  U1 = 2.4GHz Low Power Transceiver [package=qfn20]
  U2 = 2.4GHz Low Power Transceiver [package=qfn20]  # not connected
  Raspberry_Pi1 = Raspberry Pi 2  # not connected
  C1 = Capacitor Polarized [part_number=10uF package=panasonic_h13]

nets:
  N1: Arduino.ICSP_MISO, Arduino.D12/MISO, U1.MISO
  N2: Arduino.ICSP_SCK, Arduino.D13/SCK, U1.SCK
  N3: Arduino.ICSP_MOSI, Arduino.D11_PWM/MOSI, U1.MOSI
  GND: Arduino.GND, U1.VSS, C1.-
  N4: Arduino.D9_PWM, U1.CE
  N5: Arduino.D10_PWM/SS, U1.CSN
  3V3: Arduino.3V3, U1.VDD, C1.+
